# Fritzing sketch DHT11 (saved by Fritzing 0.9.3b)
breadboards: 1

parts:
  linino_one1 = linino one
  DHT1 = DHT11 Humitidy and Temperature Sensor
  R1 = Resistor [tolerance=±5% resistance=220 package=THT]

nets:
  5V: linino_one1.5V, DHT1.VDD, R1.Pin_0
  GND: linino_one1.GND, DHT1.GND
  N1: linino_one1.D2, DHT1.DATA, R1.Pin_1

notes:
  10kΩ

custom parts:
  DHT11 Humitidy and Temperature Sensor: DHT11 Humidity and Temperature Sensor
